# Fritzing sketch CyGate4 (saved by Fritzing 0.9.3b)
circuit board: 22.0481cm x 14.4169cm
breadboards: 7

parts:
  J1 = Screw terminal - 2 pins [package=THT]
  C1 = Ceramic Capacitor [capacitance=0.47mF package="100 mil [THT, multilayer]"]
  IC2 = Voltage Regulator [package=78xxl]
  IC3 = V_REG_LD1117VXX [package=78xxl]
  C2 = Tantalum Capacitor [capacitance=0.22mF voltage=10V package="100 mil [THT, tantalum]"]
  C3 = Tantalum Capacitor [capacitance=1μF voltage=10V package="100 mil [THT, tantalum]"]
  C4 = Ceramic Capacitor [capacitance=0.1mF package="100 mil [THT, multilayer]"]
  C5 = Tantalum Capacitor [capacitance=100nF package="100 mil [THT, tantalum]"]
  R1 = Resistor [tolerance=±5% resistance=150 package=THT]
  LED1 = LED - 5mm [color="Green (570nm)" package="5 mm [THT]"]
  C6 = Tantalum Capacitor [capacitance=1μF package="100 mil [THT, tantalum]"]
  IC1 = Voltage Regulator [package=to-220-alt]
  J2 = double row male pin header, 40 pins [form="♂ (male)"]
  IC4 = MCP23017 I2C I/O Expander
  R2 = Resistor [tolerance=±5% resistance=3.3k package=THT]
  C7 = Ceramic Capacitor [capacitance=1pF package="100 mil [THT, multilayer]"]
  IC5 = DS1307 [package=THT]
  BAT1 = Battery Holders [package=battcom_20mm_pth]
  XTAL1 = Crystal [frequency="32 kHz" package=THT]
  C8 = Ceramic Capacitor [capacitance=1pF package="100 mil [THT, multilayer]"]
  R3 = Resistor [tolerance=±5% resistance=10k package=THT]
  R4 = Resistor [tolerance=±5% resistance=10k package=THT]
  R5 = Resistor [tolerance=±5% resistance=10k package=THT]
  R6 = Resistor [tolerance=±5% resistance=10k package=THT]
  R7 = Resistor [tolerance=±5% resistance=10k package=THT]
  R8 = Resistor [tolerance=±5% resistance=10k package=THT]
  R9 = Resistor [tolerance=±5% resistance=10k package=THT]
  R10 = Resistor [tolerance=±5% resistance=10k package=THT]
  LED2 = LED - 5mm [color="Red (633nm)" package="5 mm [THT]"]
  R11 = Resistor [tolerance=±5% resistance=330 package=THT]
  J4 = screw terminal, 16 pins
  U1 = Sharp PC817 [package=THT]
  U2 = Sharp PC817 [package=THT]
  U3 = Sharp PC817 [package=THT]
  U4 = Sharp PC817 [package=THT]
  U5 = Sharp PC817 [package=THT]
  U6 = Sharp PC817 [package=THT]
  U7 = Sharp PC817 [package=THT]
  U8 = Sharp PC817 [package=THT]
  R12 = Resistor [tolerance=±5% resistance=1k package=THT]
  R13 = Resistor [tolerance=±5% resistance=1k package=THT]
  R14 = Resistor [tolerance=±5% resistance=1k package=THT]
  R15 = Resistor [tolerance=±5% resistance=1k package=THT]
  R16 = Resistor [tolerance=±5% resistance=1k package=THT]
  R17 = Resistor [tolerance=±5% resistance=1k package=THT]
  R18 = Resistor [tolerance=±5% resistance=1k package=THT]
  R19 = Resistor [tolerance=±5% resistance=1k package=THT]
  J3 = screw terminal, 12 pins
  IC6 = ULN2803 Darlington Array
  C9 = Ceramic Capacitor [capacitance=1pF package="100 mil [THT, multilayer]"]
  REL1 = RELAY [package=relay-jzc]
  REL2 = RELAY [package=relay-jzc]
  REL3 = RELAY [package=relay-jzc]
  REL4 = RELAY [package=relay-jzc]
  J5 = Screw terminal - 2 pins [package=THT]
  J6 = Screw terminal - 2 pins [package=THT]
  J7 = Screw terminal - 2 pins [package=THT]
  J8 = Screw terminal - 2 pins [package=THT]
  LED3 = LED - 5mm [color="Red (633nm)" package="5 mm [THT]"]
  LED4 = LED - 5mm [color="Red (633nm)" package="5 mm [THT]"]
  LED5 = LED - 5mm [color="Red (633nm)" package="5 mm [THT]"]
  LED6 = LED - 5mm [color="Red (633nm)" package="5 mm [THT]"]
  R20 = Resistor [tolerance=±5% resistance=150 package=THT]
  R21 = Resistor [tolerance=±5% resistance=150 package=THT]
  R22 = Resistor [tolerance=±5% resistance=150 package=THT]
  R23 = Resistor [tolerance=±5% resistance=150 package=THT]
  LED7 = LED - 3mm [color="Red (633nm)" package="3 mm [THT]"]
  J9 = double row male pin header, 12 pins [form="♂ (male)"]
  J10 = male pin header, 2 pins [form="♂ (male)"]
  J11 = Screw terminal - 2 pins [package=THT]
  J12 = female pin header, 4 pins [form="♀ (female)"]
  J13 = female pin header, 4 pins [form="♀ (female)"]

nets:
  N1: J1.pin1, C1.0, IC1.IN
  GND: J1.pin2, C1.1, IC2.GND, IC3.GND, C2.-, C3.-, C4.0, C5.-, R1.Pin_0, C6.-, IC1.GND, J2.pin5, J2.pin13, J2.pin20, J2.pin24, J2.pin26, J2.pin31, J2.pin34, J2.pin38, IC4.VSS, IC4.A0, IC4.A1, IC4.A2, C7.1, IC5.0V, BAT1.-, C8.0, R11.Pin_1, U1.Pin_3, U2.Pin_3, U3.Pin_3, U4.Pin_3, U5.Pin_3, U6.Pin_3, U7.Pin_3, U8.Pin_3, J3.pin2, J3.pin5, J3.pin8, J3.pin11, IC6.GND, C9.1, REL1.COIL1, REL2.COIL1, REL3.COIL1, REL4.COIL1, R20.Pin_0, R21.Pin_0, R22.Pin_0, R23.Pin_0, LED7.cathode, J9.pin1, J13.pin4
  N2: IC2.IN, C2.+, C3.+, IC1.OUT
  N3: IC2.OUT, IC3.IN, C4.1, C5.+, LED1.anode, J2.pin39, J2.pin40, J9.pin11, J13.pin1
  N4: IC3.OUT, C6.+, IC5.+V, C8.1, IC6.COMMON, C9.0, J9.pin12
  N5: R1.Pin_1, LED1.cathode
  N6: J2.pin2, IC4.SDA, IC5.SDA_-_I2C_Data, J10.pin2
  N7: J2.pin3, IC4.SCL, IC5.SCL_-_I2C_Clock, J10.pin1
  N8: J2.pin4, U1.Pin_4
  N9: J2.pin6, U2.Pin_4
  N10: J2.pin7, U3.Pin_4
  N11: J2.pin8, U4.Pin_4
  N12: J2.pin15, U5.Pin_4
  N13: J2.pin16, U6.Pin_4
  N14: J2.pin17, LED2.anode
  N15: J2.pin18, J9.pin2
  N16: J2.pin19, J9.pin3
  N17: J2.pin21, IC4.VDD, R2.Pin_1, C7.0, J9.pin4
  N18: J2.pin22, J9.pin6
  N19: J2.pin23, J9.pin5
  N20: J2.pin29, J12.pin2, J12.pin3
  N21: J2.pin30, J9.pin7
  N22: J2.pin32, J9.pin8
  N23: J2.pin33, J9.pin9
  N24: J2.pin35, J9.pin10
  N25: J2.pin36, J12.pin1
  N26: J2.pin37, J12.pin4
  N27: IC4.GPB0, IC6.I1, IC6.I5
  N28: IC4.GPB1, IC6.I2, IC6.I6
  N29: IC4.GPB2, IC6.I3, IC6.I7
  N30: IC4.GPB3, IC6.I4, IC6.I8
  N31: IC4.GPB4, LED7.anode
  N32: IC4.GPB6, U8.Pin_4
  N33: IC4.GPB7, U7.Pin_4
  N34: IC4.RESET, R2.Pin_0
  N35: IC4.GPA0, R3.Pin_0
  N36: IC4.GPA1, R4.Pin_0
  N37: IC4.GPA2, R5.Pin_0
  N38: IC4.GPA3, R6.Pin_0
  N39: IC4.GPA4, R7.Pin_0
  N40: IC4.GPA5, R8.Pin_0
  N41: IC4.GPA6, R9.Pin_0
  N42: IC4.GPA7, R10.Pin_0
  N43: IC5.X1_-_Crystal, XTAL1.pin_0
  N44: IC5.X2_-_Crystal, XTAL1.pin_1
  N45: IC5.Vbat_-_Backup_Supply, BAT1.+
  N46: R3.Pin_1, J3.pin12
  N47: R4.Pin_1, J3.pin10
  N48: R5.Pin_1, J3.pin9
  N49: R6.Pin_1, J3.pin7
  N50: R7.Pin_1, J3.pin6
  N51: R8.Pin_1, J3.pin4
  N52: R9.Pin_1, J3.pin3
  N53: R10.Pin_1, J3.pin1
  N54: LED2.cathode, R11.Pin_0
  N55: J4.pin1, R19.Pin_0
  N56: J4.pin2, U8.Pin_1
  N57: J4.pin3, R18.Pin_0
  N58: J4.pin4, U7.Pin_1
  N59: J4.pin5, R17.Pin_0
  N60: J4.pin6, U6.Pin_1
  N61: J4.pin7, R16.Pin_0
  N62: J4.pin8, U5.Pin_1
  N63: J4.pin9, R15.Pin_0
  N64: J4.pin10, U4.Pin_1
  N65: J4.pin11, R14.Pin_0
  N66: J4.pin12, U3.Pin_1
  N67: J4.pin13, R12.Pin_0
  N68: J4.pin14, U2.Pin_1
  N69: J4.pin15, R13.Pin_0
  N70: J4.pin16, U1.Pin_1
  N71: U1.Pin_2, R13.Pin_1
  N72: U2.Pin_2, R12.Pin_1
  N73: U3.Pin_2, R14.Pin_1
  N74: U4.Pin_2, R15.Pin_1
  N75: U5.Pin_2, R16.Pin_1
  N76: U6.Pin_2, R17.Pin_1
  N77: U7.Pin_2, R18.Pin_1
  N78: U8.Pin_2, R19.Pin_1
  N79: IC6.O8, REL1.COIL2
  N80: IC6.O7, REL2.COIL2
  N81: IC6.O6, REL3.COIL2
  N82: IC6.O5, REL4.COIL2
  N83: IC6.O4, LED3.anode
  N84: IC6.O3, LED4.anode
  N85: IC6.O2, LED5.anode
  N86: IC6.O1, LED6.anode
  N87: REL1.NO, J5.pin1
  N88: REL1.MAIN, J5.pin2
  N89: REL2.NO, J6.pin1
  N90: REL2.MAIN, J6.pin2
  N91: REL3.NO, J7.pin1
  N92: REL3.MAIN, J7.pin2
  N93: REL4.NO, J8.pin1
  N94: REL4.MAIN, J8.pin2
  N95: LED3.cathode, R20.Pin_1
  N96: LED4.cathode, R21.Pin_1
  N97: LED5.cathode, R22.Pin_1
  N98: LED6.cathode, R23.Pin_1
  N99: J11.pin1, J13.pin2
  N100: J11.pin2, J13.pin3

notes:
  Power Supply Section
  -
  +
  12VDC IN
  9VDC OUT
  5VDC OUT
  3.3VDC OUT
  PWR
  LM2940CT
  LM7805
  LD1117
  DC PWR
  12VDC 3A
  1
  40
  3.3V
  SDA
  SCL
  GPIO21
  DC1
  REX1
  DC2
  COM
  REX2
  DC3
  REX3
  DC4
  REX4
  Dry-Contact Zone Inputs
  CR2302 3V
  DS1307
  MCP23017
  Heartbeat
  RTC Section
  Opto-Isolated Zone Input Section
  Dry-Contact Input Section
  Opto-Isolated Zone Inputs
  Z1+
  Z1-
  Z2+
  Z2-
  Z3+
  Z3-
  Z4+
  Z4-
  Z5+
  Z5-
  Z6+
  Z6-
  Z7+
  Z7-
  Z8+
  Z8-
  GND
  Relay Section
  NO
  C
  HEARTBEAT
  ULN2803A
  5V
  GPIO4
  GPIO17
  GPIO27
  GPIO22
  GPIO13
  GPIO6
  GPIO5
  ARM
  GPIO19
  GPIO26
  GPIO20
  GPIO16
  GPIO25
  GPIO24
  GPIO23
  GPIO18
  RST
  CyGate4, 4-door access and security controller, 2.0
  FAB 002001 ASSY 002001
  CyGate4 Rev 2.0
  (c) 2022 Cyrus Brunner
  www.cyrusbuilt.net
  4-Door Access Controller
  I/O Section 1
  I/O Section 2
  A
  B
  MODBUS RS-485
  GPIO8
  TXD0
  RXD0
  VCC
  RS-485 Modbus Module
  -------------------
  RS-485
  R0
  RE
  DE
  DI
  DIO1
  DIO2
  DIO3
  DIO4
  DIO5
  DIO6
  DIO7
  DIO8
  PC817
  I/O Expansion

custom parts:
  MCP23017 I2C I/O Expander: The MCP23017 uses two i2c pins (these can be shared with other i2c devices), and in exchange gives you 16 general purpose pins. You can set each of 16 pins to be input, output, input with a pullup or open drain. There's even the ability to get an interrupt via an external pin when any of the inputs change so you don't have to keep polling the chip.
  ULN2803 Darlington Array: ULN2803 Darlington Transistor Array with Flyback Protection
