# Fritzing sketch Prox Reader Interface (saved by Fritzing 0.9.3b)
circuit board: 12.895cm x 7.79423cm
breadboards: 2

parts:
  IC1 = MCP23017 I2C I/O Expander
  R1 = Resistor [tolerance=±5% resistance=3.3k package=THT]
  J1 = male pin header, 3 pins [form="♂ (male)"]
  J2 = male pin header, 3 pins [form="♂ (male)"]
  J3 = male pin header, 3 pins [form="♂ (male)"]
  C1 = Ceramic Capacitor [capacitance=100nF package="100 mil [THT, multilayer]"]
  R2 = Resistor [tolerance=±5% resistance=4.7k package=THT]
  R3 = Resistor [tolerance=±5% resistance=4.7k package=THT]
  J4 = male pin header, 8 pins [form="♂ (male)"]
  J5 = screw terminal, 6 pins
  J6 = screw terminal, 6 pins
  J7 = screw terminal, 6 pins
  J8 = screw terminal, 6 pins
  D1 = Rectifier Diode [part_number=1N4001 package="300 mil [THT]"]
  LED1 = LED - 5mm [color="Red (633nm)" package="5 mm [THT]"]
  R4 = Resistor [tolerance=±5% resistance=150 package=THT]
  J9 = male pin header, 2 pins [form="♂ (male)"]
  J10 = male pin header, 6 pins [form="♂ (male)"]

nets:
  N1: IC1.GPB0, J6.pin6
  N2: IC1.GPB1, J7.pin6
  N3: IC1.GPB2, J8.pin6
  N4: IC1.GPB3, J10.pin4
  N5: IC1.VDD, C1.0, D1.cathode
  N6: IC1.VSS, J1.pin3, J2.pin3, J3.pin3, C1.1, J4.pin8, J5.pin1, J6.pin1, J7.pin1, J8.pin1, R4.Pin_0, J10.pin6
  N7: IC1.SCL, R3.Pin_0, J4.pin5, J9.pin2
  N8: IC1.SDA, R2.Pin_0, J4.pin6, J9.pin1
  N9: IC1.A0, J3.pin2
  N10: IC1.A1, J2.pin2
  N11: IC1.A2, J1.pin2
  N12: IC1.RESET, R1.Pin_1
  N13: IC1.GPA6, IC1.GPA7
  N14: R1.Pin_0, J1.pin1, J2.pin1, J3.pin1, R2.Pin_1, R3.Pin_1, J4.pin7, J5.pin2, J6.pin2, J7.pin2, J8.pin2, D1.anode, LED1.anode, J10.pin5
  N15: J4.pin1, J5.pin5, J6.pin5, J7.pin5, J8.pin5, J10.pin1
  N16: J4.pin2, J5.pin4, J6.pin4, J7.pin4, J8.pin4, J10.pin2
  N17: J4.pin3, J5.pin3, J6.pin3, J7.pin3, J8.pin3, J10.pin3
  N18: J4.pin4, J5.pin6
  N19: LED1.cathode, R4.Pin_1

notes:
  Gnd
  +5V
  SDA
  SCL
  CS
  MOSI
  MISO
  SCK
  A2
  A1
  A0
  I2C OUT
  ADDRESS SELECT
  INPUT FROM CYGATE
  SPI OUT
  READER 1
  READER 2
  READER 3
  READER 4
  PWR
  CyGate4 - Prox Reader Interface, Card reader and Proximity RF Card/FOB reader support, 1.0
  MCP23017
  To CyGate4
  CyGate4 Prox Reader Interface Rev 1.0
  Copyright (c) 2020 Cyrus Brunner
  www.cyrusbuilt.net
  FAB 001001 ASSY 001002

custom parts:
  MCP23017 I2C I/O Expander: The MCP23017 uses two i2c pins (these can be shared with other i2c devices), and in exchange gives you 16 general purpose pins. You can set each of 16 pins to be input, output, input with a pullup or open drain. There's even the ability to get an interrupt via an external pin when any of the inputs change so you don't have to keep polling the chip.
